# Fritzing sketch Pratica2-3 (saved by Fritzing 0.9.10b)
breadboards: 1

parts:
  Mod1 = Amica NodeMCU DEVKIT 1.0
  R1 = Resistor [tolerance=±5% power=0.25 resistance=220 package=THT]
  LED1 = LED - 5mm [color="Red (633nm)" current=0.030 package="5 mm [THT]"]
  R2 = PHOTOCELL [package=photocell-kit]

nets:
  N1: Mod1.pin1, Mod1.pin_10, Mod1.pin_26, R2.P$2
  N2: Mod1.pin2, Mod1.pin_9, Mod1.pin_25, Mod1.pin_29, LED1.cathode
  N3: Mod1.pin_13, R1.Pin_0
  N4: Mod1.pin_16, R2.P$1
  N5: R1.Pin_1, LED1.anode
